// Logisim project задание 1.circ as structural Verilog: 1 circuit, main circuit main
module main (
  input  a,
  input  b,
  input  c,
  output y
);

  wire and_1_out, and_2_out, and_3_out, nand_1_out, nand_2_out, not_1_out, not_2_out, not_3_out;

  not not_1 (not_1_out, a);
  not not_2 (not_2_out, not_1_out);
  nand nand_1 (nand_1_out, not_2_out, b);
  not not_3 (not_3_out, b);
  nand nand_2 (nand_2_out, a, b);
  and and_1 (and_1_out, nand_1_out, c);
  and and_2 (and_2_out, a, not_3_out, c);
  and and_3 (and_3_out, nand_2_out, c);
  or or_1 (y, and_1_out, and_2_out, and_3_out);
endmodule
