// Logisim project задание 2.circ as structural Verilog: 2 circuits, main circuit main
module main (
  input  A,
  input  B,
  input  C,
  output F
);

  wire and_1_out, and_2_out, and_3_out, nor_1_out;

  and and_1 (and_1_out, A, B);
  and and_2 (and_2_out, B, C);
  nor nor_1 (nor_1_out, and_1_out, and_2_out);
  and and_3 (and_3_out, A, C);
  or or_1 (F, nor_1_out, and_3_out);
endmodule

module main1 (
  input  A,
  input  B,
  input  C,
  output F
);

  wire nand_1_out, nand_2_out, nand_3_out, nand_4_out;

  nand nand_1 (nand_1_out, A, B);
  nand nand_2 (nand_2_out, B, C);
  nand nand_3 (nand_3_out, nand_1_out, nand_2_out);
  nand nand_4 (nand_4_out, A, C);
  nand nand_5 (F, nand_3_out, nand_4_out);
endmodule
