// Logisim project задание 3.circ as structural Verilog: 1 circuit, main circuit main
module main (
  input  x1,
  input  x2,
  input  x3,
  output Y1,
  output Y2
);

  wire and_1_out, not_1_out, not_2_out, or_1_out;

  not not_1 (not_1_out, x1);
  not not_2 (not_2_out, x2);
  or or_1 (or_1_out, not_1_out, not_2_out);
  and and_1 (and_1_out, x2, x3);
  or or_2 (Y1, or_1_out, x3);
  and and_2 (Y2, x1, and_1_out);
endmodule
